# Fritzing sketch epaperFrame-schematic (saved by Fritzing 0.9.6b)

parts:
  Part1 = Adafruit Feather 32u4 Adalogger [part_number="Adafruit #2795"]
  Part2 = Adafruit TPL5111 Reset Enable Timer [part_number="Adafruit #3573"]
  Part3 = Lithium Ion Polymer Battery 3.7v 500mAh [part_number=1578]  # not connected
  OLED1 = WaveShare 1.3 inch OLED
  R2 = PHOTOCELL [package=photocell-kit]
  R3 = Resistor [tolerance=±5% resistance=10k package="0402 [SMD]"]

nets:
  GND: Part1.GND, Part2.GND, OLED1.GND, R3.Pin_0
  N1: Part1.MOSI, OLED1.DIN
  N2: Part1.SCK, OLED1.CLK
  N3: Part1.A5, OLED1.CS
  N4: Part1.A4, OLED1.D/C
  N5: Part1.A3, OLED1.RES
  N6: Part1.A2, OLED1.NC
  N7: Part1.A0, R2.P$1, R3.Pin_1
  +3V3: Part1.+3V3, OLED1.VCC, R2.P$2
  N8: Part1.VBAT, Part2.VDD
  N9: Part1.EN, Part2.ENOUT
  N10: Part1.5, Part2.DONE

custom parts:
  Adafruit Feather 32u4 Adalogger: This is the Adafruit Feather 32u4 Adalogger - our take on an 'all-in-one' datalogger (or data-reader) with built in USB and battery charging. Its an Adafruit Feather 32u4 with a microSD holder ready to rock! We have other boards in the Feather family, check'em out here At the Feather 32u4's heart is at ATmega32u4 clocked at 8 MHz and at 3.3V logic, a chip setup we've had tons of experience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
  Adafruit TPL5111 Reset Enable Timer: The Adafruit TPL5111 Reset Enable Timer is a stand-alone breakout that will turn any electronics into low-power electronics! It will take care of enabling & disabling your electronics using a built in timer that can vary from once-every 100ms up to once every two hours. Basically, the TPL will set an enable pin high periodically, adjustable by potentiometer or resistor, and turn on your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
  Lithium Ion Polymer Battery 3.7v 500mAh: Lithium ion polymer (also known as 'lipo' or 'lipoly') batteries are thin, light and powerful. The output ranges from 4.2V when completely charged to 3.7V. This battery has a capacity of 500mAh for a total of about 1.9 Wh. The batteries come pre-attached with a genuine 2-pin JST-PH connector as shown and include the necessary protection circuitry.
  WaveShare 1.3 inch OLED: 128x64 Monochrom OLED Display with a SH1106 controller
